// Logisim project cpu.circ as structural Verilog: 6 circuits, main circuit main
module main (
);

  wire AddI, And, and_1_out, Beq, bitfinder_1_found, bitfinder_2_found, bitfinder_3_found, bitfinder_4_found,
       bitfinder_5_found, clock_1_out, Jump, Load, Mult, not_1_out, not_2_out, not_3_out, not_4_out, Or,
       Reset_out, Resta, Store, Suma, Tipo_R;
  wire [1:0] controlled_buffer_3_out_5;
  wire [3:0] bit_extender_1_out, bit_extender_2_out, bit_extender_3_out, bit_extender_4_out,
       controlled_buffer_3_out_2, controlled_buffer_3_out_3, controlled_buffer_3_out_4,
       controlled_buffer_4_out, controlled_buffer_5_out, controlled_buffer_5_out_2,
       controlled_buffer_5_out_3, controlled_buffer_5_out_4;
  wire [4:0] controlled_buffer_1_out, controlled_buffer_2_out, decoder_1_rs, Rd, Rs, Rt;
  wire [4:4] controlled_buffer_4_out_2;
  wire [5:0] Funct, Opcode;
  wire [7:0] A, B, C, D;
  wire [11:0] controlled_buffer_3_out;
  wire [15:0] Address;
  wire [23:0] adder_1_out, register_1_q;
  wire [25:0] JAddress;
  wire [31:0] rom_1_data;

  _7_Segment_Display u_7_segment_display_1 (
    .g(A[3]), .f(A[2]), .a(A[1]), .b(A[0]), .e(A[4]), .d(A[5]), .c(A[6]));  // open: dp
  Clock clock_1 (.out(clock_1_out));
  Multiplexer #(.width(8), .disabled(0), .enable("false")) multiplexer_1 (
    .in1(8'h5f), .out(A), .sel(Suma));  // open: in0
  Multiplexer #(.width(8), .disabled(0), .enable("false")) multiplexer_2 (
    .in1(8'h6e), .out(A), .sel(Resta));  // open: in0
  Multiplexer #(.width(8), .disabled(0), .enable("false")) multiplexer_3 (
    .in1(8'h5f), .out(A), .sel(And));  // open: in0
  Multiplexer #(.width(8), .disabled(0), .enable("false")) multiplexer_4 (.in1(8'h77), .out(A), .sel(Or));  // open: in0
  Multiplexer #(.width(8), .disabled(0), .enable("false")) multiplexer_5 (
    .in1(8'h5a), .out(A), .sel(Mult));  // open: in0
  ROM_part #(.addrWidth(24), .dataWidth(32)) rom_1 (.addr(adder_1_out), .data(rom_1_data));  // open: sel
  Register #(.width(24)) register_1 (
    .D(adder_1_out), .Q(register_1_q), .clk(clock_1_out), .clr(Reset_out));  // open: en
  Button Reset (.out(Reset_out));
  instruction Instructions (
    .Funct(Funct), .OpCode(Opcode), .Tipo_R(Tipo_R), .Suma(Suma), .Resta(Resta), .And(And), .Or(Or),
    .Mult(Mult), .Beq(Beq), .AddI(AddI), .Load(Load), .Store(Store), .Jump(Jump));
  Multiplexer #(.width(8), .disabled(0), .enable("false")) multiplexer_6 (
    .in1(8'h7c), .out(A), .sel(Beq));  // open: in0
  Multiplexer #(.width(8), .disabled(0), .enable("false")) multiplexer_7 (
    .in1(8'h5f), .out(A), .sel(AddI));  // open: in0
  Multiplexer #(.width(8), .disabled(0), .enable("false")) multiplexer_8 (
    .in1(8'h34), .out(A), .sel(Load));  // open: in0
  Multiplexer #(.width(8), .disabled(0), .enable("false")) multiplexer_9 (
    .in1(8'h6e), .out(A), .sel(Store));  // open: in0
  Multiplexer #(.width(8), .disabled(0), .enable("false")) multiplexer_10 (
    .in1(8'h61), .out(A), .sel(Jump));  // open: in0
  _7_Segment_Display u_7_segment_display_2 (
    .g(B[3]), .f(B[2]), .a(B[1]), .b(B[0]), .e(B[4]), .d(B[5]), .c(B[6]));  // open: dp
  decoder decoder_1 (
    .Address(Address), .in_1(rom_1_data), .Tipo_R(Tipo_R), .Funct(Funct), .Rd(Rd), .Rt(Rt),
    .Rs(decoder_1_rs), .OpCode(Opcode), .JAddress(JAddress));
  Adder #(.width(24)) adder_1 (.a(24'h1), .b(register_1_q), .out(adder_1_out));  // open: cin, cout
  Multiplexer #(.width(8), .disabled(0), .enable("false")) multiplexer_11 (
    .in1(8'h79), .out(B), .sel(Suma));  // open: in0
  Multiplexer #(.width(8), .disabled(0), .enable("false")) multiplexer_12 (
    .in1(8'h75), .out(B), .sel(Resta));  // open: in0
  Multiplexer #(.width(8), .disabled(0), .enable("false")) multiplexer_13 (
    .in1(8'h57), .out(B), .sel(And));  // open: in0
  Multiplexer #(.width(8), .disabled(0), .enable("false")) multiplexer_14 (
    .in1(8'h16), .out(B), .sel(Or));  // open: in0
  Multiplexer #(.width(8), .disabled(0), .enable("false")) multiplexer_15 (
    .in1(8'h75), .out(B), .sel(Mult));  // open: in0
  _7_Segment_Display u_7_segment_display_3 (
    .g(C[3]), .f(C[2]), .a(C[1]), .b(C[0]), .e(C[4]), .d(C[5]), .c(C[6]));  // open: dp
  Hex_Digit_Display hex_digit_display_1 (.value(bit_extender_1_out));  // open: dp
  assign bit_extender_1_out = {{2{1'b0}}, controlled_buffer_3_out_5};  // Bit_Extender bit_extender_1
  Multiplexer #(.width(8), .disabled(0), .enable("false")) multiplexer_16 (
    .in1(8'h3f), .out(B), .sel(Beq));  // open: in0
  Multiplexer #(.width(8), .disabled(0), .enable("false")) multiplexer_17 (
    .in1(8'h79), .out(B), .sel(AddI));  // open: in0
  Multiplexer #(.width(8), .disabled(0), .enable("false")) multiplexer_18 (
    .in1(8'h77), .out(B), .sel(Load));  // open: in0
  Multiplexer #(.width(8), .disabled(0), .enable("false")) multiplexer_19 (
    .in1(8'h3c), .out(B), .sel(Store));  // open: in0
  Multiplexer #(.width(8), .disabled(0), .enable("false")) multiplexer_20 (
    .in1(8'h75), .out(B), .sel(Jump));  // open: in0
  _7_Segment_Display u_7_segment_display_4 (
    .g(D[3]), .f(D[2]), .a(D[1]), .b(D[0]), .e(D[4]), .d(D[5]), .c(D[6]));  // open: dp
  Hex_Digit_Display hex_digit_display_2 (.value(controlled_buffer_3_out_4));  // open: dp
  Multiplexer #(.width(8), .disabled(0), .enable("false")) multiplexer_21 (
    .in1(8'h79), .out(C), .sel(Suma));  // open: in0
  Multiplexer #(.width(8), .disabled(0), .enable("false")) multiplexer_22 (
    .in1(8'h7c), .out(C), .sel(Resta));  // open: in0
  Multiplexer #(.width(8), .disabled(0), .enable("false")) multiplexer_23 (
    .in1(8'h79), .out(C), .sel(And));  // open: in0
  Multiplexer #(.width(8), .disabled(0), .enable("false")) multiplexer_24 (
    .in1(8'h34), .out(C), .sel(Mult));  // open: in0
  Hex_Digit_Display hex_digit_display_3 (.value(bit_extender_2_out));  // open: dp
  assign bit_extender_2_out = {{3{1'b0}}, controlled_buffer_1_out[4]};  // Bit_Extender bit_extender_2
  not not_1 (not_1_out, Jump);
  assign controlled_buffer_1_out = bitfinder_1_found ? Rs : 5'bz;  // Controlled_Buffer controlled_buffer_1
  Hex_Digit_Display hex_digit_display_4 (.value(controlled_buffer_3_out_2));  // open: dp
  Hex_Digit_Display hex_digit_display_5 (.value(controlled_buffer_3_out_3));  // open: dp
  Multiplexer #(.width(8), .disabled(0), .enable("false")) multiplexer_25 (
    .in1(8'h4f), .out(C), .sel(Beq));  // open: in0
  Multiplexer #(.width(8), .disabled(0), .enable("false")) multiplexer_26 (
    .in1(8'h79), .out(C), .sel(AddI));  // open: in0
  Multiplexer #(.width(8), .disabled(0), .enable("false")) multiplexer_27 (
    .in1(8'h5f), .out(C), .sel(Load));  // open: in0
  Multiplexer #(.width(8), .disabled(0), .enable("false")) multiplexer_28 (
    .in1(8'h5a), .out(C), .sel(Jump));  // open: in0
  Hex_Digit_Display hex_digit_display_6 (.value(controlled_buffer_1_out[3:0]));  // open: dp
  assign controlled_buffer_2_out = bitfinder_2_found ? Rt : 5'bz;  // Controlled_Buffer controlled_buffer_2
  BitFinder #(.width(1)) bitfinder_1 (.in(not_1_out), .found(bitfinder_1_found));  // open: index
  Hex_Digit_Display hex_digit_display_7 (.value(controlled_buffer_3_out[11:8]));  // open: dp
  assign {controlled_buffer_3_out_5, controlled_buffer_3_out_4, controlled_buffer_3_out_3, controlled_buffer_3_out_2, controlled_buffer_3_out} = bitfinder_3_found ? JAddress : 26'bz;  // Controlled_Buffer controlled_buffer_3
  Multiplexer #(.width(8), .disabled(0), .enable("false")) multiplexer_29 (
    .in1(8'h14), .out(D), .sel(AddI));  // open: in0
  Multiplexer #(.width(8), .disabled(0), .enable("false")) multiplexer_30 (
    .in1(8'h79), .out(D), .sel(Load));  // open: in0
  Multiplexer #(.width(8), .disabled(0), .enable("false")) multiplexer_31 (
    .in1(8'h3c), .out(D), .sel(Mult));  // open: in0
  Multiplexer #(.width(8), .disabled(0), .enable("false")) multiplexer_32 (
    .in1(8'h1f), .out(D), .sel(Jump));  // open: in0
  Hex_Digit_Display hex_digit_display_8 (.value(bit_extender_3_out));  // open: dp
  Hex_Digit_Display hex_digit_display_9 (.value(controlled_buffer_2_out[3:0]));  // open: dp
  assign bit_extender_3_out = {{3{1'b0}}, controlled_buffer_2_out[4]};  // Bit_Extender bit_extender_3
  not not_2 (not_2_out, Jump);
  Hex_Digit_Display hex_digit_display_10 (.value(controlled_buffer_3_out[7:4]));  // open: dp
  Hex_Digit_Display hex_digit_display_11 (.value(bit_extender_4_out));  // open: dp
  assign bit_extender_4_out = {{3{1'b0}}, controlled_buffer_4_out_2[4]};  // Bit_Extender bit_extender_4
  assign {controlled_buffer_4_out_2[4], controlled_buffer_4_out} = bitfinder_4_found ? Rd : 5'bz;  // Controlled_Buffer controlled_buffer_4
  BitFinder #(.width(1)) bitfinder_2 (.in(not_2_out), .found(bitfinder_2_found));  // open: index
  Hex_Digit_Display hex_digit_display_12 (.value(controlled_buffer_5_out_4));  // open: dp
  Hex_Digit_Display hex_digit_display_13 (.value(controlled_buffer_3_out[3:0]));  // open: dp
  BitFinder #(.width(1)) bitfinder_3 (.in(Jump), .found(bitfinder_3_found));  // open: index
  Hex_Digit_Display hex_digit_display_14 (.value(controlled_buffer_4_out));  // open: dp
  BitFinder #(.width(1)) bitfinder_4 (.in(Tipo_R), .found(bitfinder_4_found));  // open: index
  Hex_Digit_Display hex_digit_display_15 (.value(controlled_buffer_5_out_3));  // open: dp
  Hex_Digit_Display hex_digit_display_16 (.value(controlled_buffer_5_out_2));  // open: dp
  assign {controlled_buffer_5_out_4, controlled_buffer_5_out_3, controlled_buffer_5_out_2, controlled_buffer_5_out} = bitfinder_5_found ? Address : 16'bz;  // Controlled_Buffer controlled_buffer_5
  not not_3 (not_3_out, Tipo_R);
  and and_1 (and_1_out, not_3_out, not_4_out);
  not not_4 (not_4_out, Jump);
  Hex_Digit_Display hex_digit_display_17 (.value(controlled_buffer_5_out));  // open: dp
  BitFinder #(.width(1)) bitfinder_5 (.in(and_1_out), .found(bitfinder_5_found));  // open: index

  // Notes on the sheet:
  //   contents of rom_1 (hex, n*v repeats v):
  //   12c6820 11a00001 1a90020 8c890001 1397020 8100008 120c820 329c824 13200001 810000c 20 1019fff7
  //   1495020
  //   Instruction
  //   Decoder
  //   rs
  //   Jump Address
  //   rt
  //   rd
  //   Address
endmodule

module decoder (
  input  [31:0] in_1,
  output Tipo_R,
  output [15:0] Address,
  output [5:0] Funct,
  output [4:0] Rd,
  output [4:0] Rt,
  output [4:0] Rs,
  output [5:0] OpCode,
  output [25:0] JAddress
);

  Comparator #(.width(6)) comparator_1 (.a(in_1[31:26]), .b({6{1'b0}}), .eq(Tipo_R));  // open: gt, lt

  assign Address = in_1[15:0];
  assign Funct = in_1[5:0];
  assign JAddress = in_1[25:0];
  assign OpCode = in_1[31:26];
  assign Rd = in_1[15:11];
  assign Rs = in_1[25:21];
  assign Rt = in_1[20:16];
endmodule

module pc (
  input  clk,
  output [31:0] data
);

  wire [7:0] register_1_q_2;
  wire [23:0] register_1_q;
  wire [31:0] adder_1_out;

  Register #(.width(32)) register_1 (.D(adder_1_out), .Q({register_1_q_2, register_1_q}), .clk(clk));  // open: en, clr
  Adder #(.width(32)) adder_1 (.a(32'h1), .b({register_1_q_2, register_1_q}), .out(adder_1_out));  // open: cin, cout
  ROM rom_1 (.pos(register_1_q), .data(data));  // open: sel
endmodule

module RAM (
  input  [23:0] pos,
  input  [31:0] data,
  input  sel,
  input  clk,
  input  ld,
  input  clr
);

  RAM_part #(.addrWidth(24), .dataWidth(32)) ram_1 (.addr(pos), .data(data), .sel(sel), .clk(clk), .ld(ld), .clr(clr));
endmodule

module ROM (
  input  [23:0] pos,
  input  sel,
  output [31:0] data
);

  ROM_part #(.addrWidth(24), .dataWidth(32)) rom_1 (.addr(pos), .data(data), .sel(sel));
endmodule

module instruction (
  input  [5:0] Funct,
  input  [5:0] OpCode,
  input  Tipo_R,
  output Suma,
  output Resta,
  output And,
  output Or,
  output Mult,
  output Beq,
  output AddI,
  output Load,
  output Store,
  output Jump
);

  wire comparator_1_eq, comparator_2_eq, comparator_3_eq, comparator_4_eq, comparator_5_eq, comparator_6_eq,
       comparator_7_eq, comparator_8_eq, comparator_9_eq, comparator_10_eq, not_1_out, not_2_out, not_3_out,
       not_4_out, not_5_out;

  Comparator #(.width(6)) comparator_1 (.a(Funct), .b(6'b100000), .eq(comparator_1_eq));  // open: gt, lt
  not not_1 (not_1_out, Tipo_R);
  Comparator #(.width(6)) comparator_2 (.a(OpCode), .b(6'b000100), .eq(comparator_2_eq));  // open: gt, lt
  not not_2 (not_2_out, Tipo_R);
  Comparator #(.width(6)) comparator_3 (.a(OpCode), .b(6'b000010), .eq(comparator_3_eq));  // open: gt, lt
  and and_1 (Suma, Tipo_R, comparator_1_eq);
  and and_2 (Beq, not_1_out, comparator_2_eq);
  and and_3 (Jump, not_2_out, comparator_3_eq);
  Comparator #(.width(6)) comparator_4 (.a(Funct), .b(6'b100010), .eq(comparator_4_eq));  // open: gt, lt
  Comparator #(.width(6)) comparator_5 (.a(OpCode), .b(6'b001000), .eq(comparator_5_eq));  // open: gt, lt
  and and_4 (Resta, Tipo_R, comparator_4_eq);
  not not_3 (not_3_out, Tipo_R);
  and and_5 (AddI, not_3_out, comparator_5_eq);
  Comparator #(.width(6)) comparator_6 (.a(Funct), .b(6'b100100), .eq(comparator_6_eq));  // open: gt, lt
  and and_6 (And, Tipo_R, comparator_6_eq);
  not not_4 (not_4_out, Tipo_R);
  Comparator #(.width(6)) comparator_7 (.a(OpCode), .b(6'b100011), .eq(comparator_7_eq));  // open: gt, lt
  and and_7 (Load, not_4_out, comparator_7_eq);
  Comparator #(.width(6)) comparator_8 (.a(Funct), .b(6'b100101), .eq(comparator_8_eq));  // open: gt, lt
  Comparator #(.width(6)) comparator_9 (.a(OpCode), .b(6'b101011), .eq(comparator_9_eq));  // open: gt, lt
  and and_8 (Or, Tipo_R, comparator_8_eq);
  not not_5 (not_5_out, Tipo_R);
  and and_9 (Store, not_5_out, comparator_9_eq);
  Comparator #(.width(6)) comparator_10 (.a(Funct), .b(6'b011000), .eq(comparator_10_eq));  // open: gt, lt
  and and_10 (Mult, Tipo_R, comparator_10_eq);
endmodule
